// Logisim project Datapath.circ as structural Verilog
module Register (
  input  [2:0] RY,
  input  [31:0] BusX,
  input  [2:0] RZ,
  input  [2:0] RX2,
  input  [2:0] RX,
  input  RegWrite,
  input  CLK,
  output [31:0] BusY,
  output [31:0] BusZ,
  output [31:0] BusXout
);

  wire and_1_out, and_2_out, and_3_out, and_4_out, and_5_out, and_6_out, and_7_out, decoder_1_out0,
       decoder_1_out1, decoder_1_out2, decoder_1_out3, decoder_1_out4, decoder_1_out5, decoder_1_out6,
       decoder_1_out7, decoder_2_out0, decoder_2_out1, decoder_2_out2, decoder_2_out3, decoder_2_out4,
       decoder_2_out5, decoder_2_out6, decoder_2_out7, decoder_3_out0, decoder_3_out1, decoder_3_out2,
       decoder_3_out3, decoder_3_out4, decoder_3_out5, decoder_3_out6, decoder_3_out7, decoder_4_out0,
       decoder_4_out1, decoder_4_out2, decoder_4_out3, decoder_4_out4, decoder_4_out5, decoder_4_out6,
       decoder_4_out7;
  wire [31:0] R1_q, R2_q, R3_q, R4_q, R5_q, R6_q, R7_q;

  Decoder #(.select(3), .enable("false")) decoder_1 (
    .out0(decoder_1_out0), .out1(decoder_1_out1), .out2(decoder_1_out2), .out3(decoder_1_out3),
    .out4(decoder_1_out4), .out5(decoder_1_out5), .out6(decoder_1_out6), .out7(decoder_1_out7), .sel(RX));
  and and_1 (and_1_out, decoder_1_out1, RegWrite);
  and and_2 (and_2_out, decoder_1_out2, RegWrite);
  and and_3 (and_3_out, decoder_1_out3, RegWrite);
  and and_4 (and_4_out, decoder_1_out4, RegWrite);
  and and_5 (and_5_out, decoder_1_out5, RegWrite);
  and and_6 (and_6_out, decoder_1_out6, RegWrite);
  and and_7 (and_7_out, decoder_1_out7, RegWrite);
  Register_part #(.width(32)) R1 (.D(BusX), .en(and_1_out), .Q(R1_q), .clk(CLK));  // open: clr
  Register_part #(.width(32)) R2 (.D(BusX), .en(and_2_out), .Q(R2_q), .clk(CLK));  // open: clr
  Register_part #(.width(32)) R3 (.D(BusX), .en(and_3_out), .Q(R3_q), .clk(CLK));  // open: clr
  Register_part #(.width(32)) R4 (.D(BusX), .en(and_4_out), .Q(R4_q), .clk(CLK));  // open: clr
  Register_part #(.width(32)) R5 (.D(BusX), .en(and_5_out), .Q(R5_q), .clk(CLK));  // open: clr
  Register_part #(.width(32)) R6 (.D(BusX), .en(and_6_out), .Q(R6_q), .clk(CLK));  // open: clr
  Register_part #(.width(32)) R7 (.D(BusX), .en(and_7_out), .Q(R7_q), .clk(CLK));  // open: clr
  assign BusY = decoder_2_out0 ? {32{1'b0}} : 32'bz;  // Controlled_Buffer controlled_buffer_1
  assign BusY = decoder_2_out1 ? R1_q : 32'bz;  // Controlled_Buffer controlled_buffer_2
  assign BusY = decoder_2_out2 ? R2_q : 32'bz;  // Controlled_Buffer controlled_buffer_3
  assign BusY = decoder_2_out3 ? R3_q : 32'bz;  // Controlled_Buffer controlled_buffer_4
  assign BusY = decoder_2_out4 ? R4_q : 32'bz;  // Controlled_Buffer controlled_buffer_5
  assign BusY = decoder_2_out5 ? R5_q : 32'bz;  // Controlled_Buffer controlled_buffer_6
  assign BusY = decoder_2_out6 ? R6_q : 32'bz;  // Controlled_Buffer controlled_buffer_7
  assign BusY = decoder_2_out7 ? R7_q : 32'bz;  // Controlled_Buffer controlled_buffer_8
  Decoder #(.select(3), .enable("false")) decoder_2 (
    .out0(decoder_2_out0), .out1(decoder_2_out1), .out2(decoder_2_out2), .out3(decoder_2_out3),
    .out4(decoder_2_out4), .out5(decoder_2_out5), .out6(decoder_2_out6), .out7(decoder_2_out7), .sel(RY));
  Decoder #(.select(3), .enable("false")) decoder_3 (
    .out0(decoder_3_out0), .out1(decoder_3_out1), .out2(decoder_3_out2), .out3(decoder_3_out3),
    .out4(decoder_3_out4), .out5(decoder_3_out5), .out6(decoder_3_out6), .out7(decoder_3_out7), .sel(RZ));
  assign BusZ = decoder_3_out0 ? {32{1'b0}} : 32'bz;  // Controlled_Buffer controlled_buffer_9
  assign BusZ = decoder_3_out1 ? R1_q : 32'bz;  // Controlled_Buffer controlled_buffer_10
  assign BusZ = decoder_3_out2 ? R2_q : 32'bz;  // Controlled_Buffer controlled_buffer_11
  assign BusZ = decoder_3_out3 ? R3_q : 32'bz;  // Controlled_Buffer controlled_buffer_12
  assign BusZ = decoder_3_out4 ? R4_q : 32'bz;  // Controlled_Buffer controlled_buffer_13
  assign BusZ = decoder_3_out5 ? R5_q : 32'bz;  // Controlled_Buffer controlled_buffer_14
  assign BusZ = decoder_3_out6 ? R6_q : 32'bz;  // Controlled_Buffer controlled_buffer_15
  assign BusZ = decoder_3_out7 ? R7_q : 32'bz;  // Controlled_Buffer controlled_buffer_16
  assign BusXout = decoder_4_out0 ? {32{1'b0}} : 32'bz;  // Controlled_Buffer controlled_buffer_17
  assign BusXout = decoder_4_out1 ? R1_q : 32'bz;  // Controlled_Buffer controlled_buffer_18
  assign BusXout = decoder_4_out2 ? R2_q : 32'bz;  // Controlled_Buffer controlled_buffer_19
  assign BusXout = decoder_4_out3 ? R3_q : 32'bz;  // Controlled_Buffer controlled_buffer_20
  assign BusXout = decoder_4_out4 ? R4_q : 32'bz;  // Controlled_Buffer controlled_buffer_21
  assign BusXout = decoder_4_out5 ? R5_q : 32'bz;  // Controlled_Buffer controlled_buffer_22
  assign BusXout = decoder_4_out6 ? R6_q : 32'bz;  // Controlled_Buffer controlled_buffer_23
  assign BusXout = decoder_4_out7 ? R7_q : 32'bz;  // Controlled_Buffer controlled_buffer_24
  Decoder #(.select(3), .enable("false")) decoder_4 (
    .out0(decoder_4_out0), .out1(decoder_4_out1), .out2(decoder_4_out2), .out3(decoder_4_out3),
    .out4(decoder_4_out4), .out5(decoder_4_out5), .out6(decoder_4_out6), .out7(decoder_4_out7), .sel(RX2));
endmodule

module ALU (
  input  [31:0] A,
  input  [31:0] B,
  input  [3:0] Sel,
  output [31:0] Out
);

  wire comparator_1_eq, comparator_1_lt;
  wire [31:0] adder_1_out, and_1_out, and_2_out, bit_extender_1_out, bit_extender_2_out, not_1_out, or_1_out,
       shifter_1_out, shifter_2_out, shifter_3_out, shifter_4_out, subtractor_1_out, xor_1_out;

  assign not_1_out = ~A;  // NOT_Gate not_1, 32 bits wide
  assign xor_1_out = A ^ B;  // XOR_Gate xor_1, 32 bits wide
  assign and_1_out = A & B;  // AND_Gate and_1, 32 bits wide
  assign or_1_out = A | B;  // OR_Gate or_1, 32 bits wide
  assign and_2_out = not_1_out & B;  // AND_Gate and_2, 32 bits wide
  Adder #(.width(32)) adder_1 (.a(A), .b(B), .out(adder_1_out), .cin(1'b0));  // open: cout
  Comparator #(.width(32)) comparator_1 (.a(A), .b(B), .eq(comparator_1_eq), .lt(comparator_1_lt));  // open: gt
  Subtractor #(.width(32)) subtractor_1 (.a(B), .b(A), .out(subtractor_1_out), .bin(1'b0));  // open: bout
  assign bit_extender_1_out = {{31{1'b0}}, comparator_1_lt};  // Bit_Extender bit_extender_1
  Shifter #(.width(32), .shift("ar")) shifter_1 (.in(A), .\dist (B[4:0]), .out(shifter_1_out));
  Shifter #(.width(32), .shift("lr")) shifter_2 (.in(A), .\dist (B[4:0]), .out(shifter_2_out));
  Shifter #(.width(32)) shifter_3 (.in(A), .\dist (B[4:0]), .out(shifter_3_out));
  Shifter #(.width(32), .shift("rr")) shifter_4 (.in(A), .\dist (B[4:0]), .out(shifter_4_out));
  assign bit_extender_2_out = {{31{1'b0}}, comparator_1_eq};  // Bit_Extender bit_extender_2
  Multiplexer #(.select(4), .width(32), .enable("false")) multiplexer_1 (
    .in0(xor_1_out), .in1(and_1_out), .in2(or_1_out), .in3(and_2_out), .in4(adder_1_out),
    .in5(bit_extender_2_out), .in6(subtractor_1_out), .in7(bit_extender_1_out), .in8(shifter_1_out),
    .in9(shifter_2_out), .in10(shifter_3_out), .in11(shifter_4_out), .in12({32{1'b0}}), .in13({32{1'b0}}),
    .in14({32{1'b0}}), .in15({32{1'b0}}), .out(Out), .sel(Sel));
endmodule

// ControlUnit
module DataPath (
  output [31:0] out_1,
  output [31:0] out_2,
  output [31:0] out_3
);

  wire ALU_LSB, CLK_out, ImmSel, MemRead, MemWrite, RegDst, RegWrite;
  wire [1:0] f, OutputSel, PCSel;
  wire [2:0] BSel, Imm3, multiplexer_2_out;
  wire [3:0] ALUSel;
  wire [4:0] op, shifter_1_out;
  wire [4:2] Imm5;
  wire [7:5] Imm11;
  wire [10:0] shifter_2_out, shifter_3_out;
  wire [19:0] adder_1_out, adder_2_out, bit_extender_1_out, bit_extender_2_out, multiplexer_1_out, PC_2,
       PC_q, undriven;
  wire [31:0] bit_extender_6_out, bit_extender_7_out, BusXout, multiplexer_3_out, ram_1_data,
       register_1_busz, SignExtend, SW, undriven_2, ZeroExtend;
  wire [31:1] alu_1_out;

  ControlUnit controlunit_1 (
    .OpCode(op), .OutputSel(OutputSel), .MemRead(MemRead), .MemWrite(MemWrite), .BSel(BSel), .ImmSel(ImmSel),
    .RegWrite(RegWrite), .RegDst(RegDst), .F(f), .ALUSel(ALUSel), .PCSel(PCSel), .ALU_LSB(ALU_LSB));
  Shifter #(.width(5)) shifter_1 (.in({Imm5, f}), .\dist (3'b001), .out(shifter_1_out));
  assign bit_extender_1_out = {{15{shifter_1_out[4]}}, shifter_1_out};  // Bit_Extender bit_extender_1
  Shifter #(.width(11)) shifter_2 (.in({Imm3, Imm11, Imm5, f}), .\dist (4'b0001), .out(shifter_2_out));
  assign bit_extender_2_out = {{9{shifter_2_out[10]}}, shifter_2_out};  // Bit_Extender bit_extender_2
  Adder #(.width(20)) adder_1 (.a(PC_q), .b(bit_extender_1_out), .out(adder_1_out), .cin(1'b0));  // open: cout
  Adder #(.width(20)) adder_2 (.a(PC_q), .b(bit_extender_2_out), .out(adder_2_out), .cin(1'b0));  // open: cout
  Adder #(.width(20)) adder_3 (.a(PC_q), .b(20'h2), .out(PC_2), .cin(1'b0));  // open: cout
  Multiplexer #(.select(2), .width(20), .enable("false")) multiplexer_1 (
    .in0(PC_2), .in1(adder_1_out), .in2(adder_2_out), .in3(undriven), .out(multiplexer_1_out), .sel(PCSel));
  Clock CLK (.out(CLK_out));
  Register_part #(.width(20)) PC (.D(multiplexer_1_out), .en(1'b1), .Q(PC_q), .clk(CLK_out));  // open: clr
  ROM #(.addrWidth(20), .dataWidth(16)) rom_1 (.addr(PC_q), .data({op, Imm3, Imm11, Imm5, f}));  // open: sel
  Multiplexer #(.width(3), .enable("false")) multiplexer_2 (
    .in0(Imm3), .in1(3'b111), .out(multiplexer_2_out), .sel(RegDst));
  assign SW = {{27{1'b0}}, {Imm3, f}};  // Bit_Extender bit_extender_3
  Register register_1 (
    .RY(Imm11), .BusX(out_3), .RZ(Imm5), .RX(multiplexer_2_out), .RegWrite(RegWrite), .BusY(out_2),
    .BusZ(register_1_busz), .CLK(CLK_out), .RX2(Imm3), .BusXout(BusXout));
  assign ZeroExtend = {{27{1'b0}}, {Imm5, f}};  // Bit_Extender bit_extender_4
  assign SignExtend = {{27{Imm5[4]}}, {Imm5, f}};  // Bit_Extender bit_extender_5
  Multiplexer #(.width(32), .enable("false")) multiplexer_3 (
    .in0(ZeroExtend), .in1(SignExtend), .out(multiplexer_3_out), .sel(ImmSel));
  Multiplexer #(.select(3), .width(32), .enable("false")) multiplexer_4 (
    .in0(register_1_busz), .in1(multiplexer_3_out), .in2(SW), .in3(bit_extender_6_out), .in4(BusXout),
    .out(out_1), .sel(BSel));  // open: in5, in6, in7
  ALU alu_1 (.A(out_2), .B(out_1), .Out({alu_1_out, ALU_LSB}), .Sel(ALUSel));
  assign bit_extender_6_out = {{21{shifter_3_out[10]}}, shifter_3_out};  // Bit_Extender bit_extender_6
  Shifter #(.width(11)) shifter_3 (.in({Imm3, Imm11, Imm5, f}), .\dist (4'b0001), .out(shifter_3_out));
  RAM #(.addrWidth(20), .dataWidth(32), .bus("separate")) ram_1 (
    .addr({alu_1_out[19:1], ALU_LSB}), .din(register_1_busz), .data(ram_1_data), .str(MemWrite),
    .clk(CLK_out), .ld(MemRead));  // open: sel, clr
  assign bit_extender_7_out = {{12{1'b0}}, PC_2};  // Bit_Extender bit_extender_7
  Multiplexer #(.select(2), .width(32), .enable("false")) multiplexer_5 (
    .in0({alu_1_out, ALU_LSB}), .in1(ram_1_data), .in2(bit_extender_7_out), .in3(undriven_2), .out(out_3),
    .sel(OutputSel));

  // Other names for the same wires on the sheet: Imm11 (some bits) = {Imm3, Imm5, f}; z[2:0] = Imm5; y[2:0] = Imm11;
  //   Imm2[1:0] = f; Imm5[1:0] = f; x[2:0] = Imm3; BusY[31:0] = out_2

  // Notes on the sheet:
  //   contents of rom_1 (hex, n*v repeats v):
  //   91a0 0 93a1 0 91a0 0 92a1 0 0 0 7143 0 7213 0 7263 5*0 7263 5*0 7263 5*0 7a61 0 7962 0 0 0 8142 0 0
  //   0 8222 0 8a22 0 0 0 8922 0 0 0 8942 0 a004 7*0 a802
  //   BusX
  //   A
  //   B
endmodule

module ControlUnit (
  input  [4:0] OpCode,
  input  [1:0] F,
  input  ALU_LSB,
  output [1:0] OutputSel,
  output MemRead,
  output MemWrite,
  output [2:0] BSel,
  output ImmSel,
  output RegWrite,
  output RegDst,
  output [3:0] ALUSel,
  output [1:0] PCSel
);

  ROM #(.addrWidth(5), .dataWidth(10)) rom_1 (
    .addr(OpCode), .data({RegDst, RegWrite, ImmSel, BSel, MemWrite, MemRead, OutputSel}));  // open: sel
  ROM #(.addrWidth(7), .dataWidth(4)) rom_2 (.addr({OpCode, F}), .data(ALUSel));  // open: sel
  ROM #(.addrWidth(6), .dataWidth(2)) rom_3 (.addr({OpCode, ALU_LSB}), .data(PCSel));  // open: sel

  // Notes on the sheet:
  //   contents of rom_1 (hex, n*v repeats v):
  //   100 100 4*110 4*190 4*110 4*40 195 2b 73 372
  //   contents of rom_2 (hex, n*v repeats v):
  //   1 3 2 0 4 6 5 7 4*1 4*3 4*2 4*0 4*4 4*6 4*5 4*7 4*a 4*9 4*8 4*b 8*5 8*7 8*4
  //   contents of rom_3 (hex, n*v repeats v):
  //   29*0 1 1 0 0 1 1 5*0 4*2
endmodule
